# Fritzing sketch vu2 advanced (saved by Fritzing 0.9.4)
breadboards: 1

parts:
  Part1 = Arduino Uno (Rev3)
  U1 = WS2812 RGB LED strip
  JACK1 = 2.1mm Barrel Jack with Terminal Block
  TRS1 = Audio Jack (TRS) 3.5mm [package="4Ucon 08780 [THT]"]
  R2 = Resistor [tolerance=±5% resistance=330 package="0402 [SMD]"]
  C6 = Electrolytic Capacitor [capacitance=100µF package="200 mil [THT, electrolytic]"]
  S1 = Pushbutton [package="[THT]"]
  R3 = Resistor [tolerance=±5% resistance=10k package="0402 [SMD]"]
  R4 = Resistor [tolerance=±5% resistance=100k package=THT]
  C9 = Electrolytic Capacitor [capacitance=47µF package="100 mil [THT, electrolytic]"]
  R5 = Resistor [tolerance=±5% resistance=100k package=THT]
  R6 = Resistor [tolerance=±5% resistance=10k package=THT]
  R7 = Resistor [tolerance=±5% resistance=10k package=THT]
  C11 = Ceramic Capacitor [capacitance=10nF package="200 mil [THT, multilayer]"]
  R8 = Resistor [tolerance=±5% resistance=220 package="0402 [SMD]"]
  R9 = Resistor [tolerance=±5% resistance=220 package="0402 [SMD]"]
  LED2 = LED - 3mm [color="Yellow (595nm)" package="3 mm [THT]"]
  LED5 = LED - 3mm [color="Green (570nm)" package="3 mm [THT]"]
  LED6 = LED - 3mm [color="Green (570nm)" package="3 mm [THT]"]
  LED7 = LED - 3mm [color="Green (570nm)" package="3 mm [THT]"]
  LED8 = LED - 3mm [color="Yellow (595nm)" package="3 mm [THT]"]
  LED9 = LED - 3mm [color="Green (570nm)" package="3 mm [THT]"]

nets:
  N1: Part1.A0, C9.-
  N2: Part1.D8, LED5.anode
  N3: Part1.D9_PWM, LED6.anode
  N4: Part1.D10_PWM/SS, LED7.anode
  N5: Part1.D11_PWM/MOSI, LED9.anode
  N6: Part1.D2, LED2.anode
  N7: Part1.D3_PWM, LED8.anode
  N8: Part1.D4, S1.Pin_3, S1.Pin_4, R3.Pin_1
  N9: Part1.D6_PWM, R2.Pin_1
  5V: Part1.5V, U1.VCC, JACK1.POS, C6.+, S1.Pin_1, S1.Pin_2, R4.Pin_1
  GND: Part1.GND, U1.GND, JACK1.NEG, TRS1.Sleeve, C6.-, R3.Pin_0, R5.Pin_1, R6.Pin_1, R7.Pin_1, C11.0, R8.Pin_1, R9.Pin_0, LED5.cathode, LED6.cathode, LED7.cathode, LED9.cathode
  N10: U1.DIN, R2.Pin_0
  N11: TRS1.Ring, R4.Pin_0, C9.+, R5.Pin_0, C11.1
  N12: R8.Pin_0, LED2.cathode
  N13: R9.Pin_1, LED8.cathode

custom parts:
  WS2812 RGB LED strip: WS2812 strip
