# Fritzing sketch vu2 basic (saved by Fritzing 0.9.4)
breadboards: 1

parts:
  Part1 = Arduino Uno (Rev3)
  U1 = WS2812 RGB LED strip
  JACK1 = 2.1mm Barrel Jack with Terminal Block
  R1 = Resistor [tolerance=±5% resistance=10k package="0402 [SMD]"]
  TRS1 = Audio Jack (TRS) 3.5mm [package="4Ucon 08780 [THT]"]
  R2 = Resistor [tolerance=±5% resistance=330 package="0402 [SMD]"]
  C6 = Electrolytic Capacitor [capacitance=100µF package="200 mil [THT, electrolytic]"]
  S1 = Pushbutton [package="[THT]"]
  R3 = Resistor [tolerance=±5% resistance=10k package="0402 [SMD]"]

nets:
  N1: Part1.A0, R1.Pin_0, TRS1.Ring
  GND: Part1.D2, Part1.D3_PWM, Part1.GND, U1.GND, JACK1.NEG, R1.Pin_1, TRS1.Sleeve, C6.-, R3.Pin_0
  N2: Part1.D4, S1.Pin_3, S1.Pin_4, R3.Pin_1
  N3: Part1.D6_PWM, R2.Pin_1
  5V: Part1.5V, U1.VCC, JACK1.POS, C6.+, S1.Pin_1, S1.Pin_2
  N4: U1.DIN, R2.Pin_0

custom parts:
  WS2812 RGB LED strip: WS2812 strip
